# Fritzing sketch GODWIN CIRCUIT (saved by Fritzing 0.9.3b)

parts:
  Part1 = Arduino Uno (Rev3) - ICSP
  Part2 = Arduino Uno (Rev3) - ICSP
  M1 = DC Motor
  M2 = DC Motor
  LCD1 = LCD screen
  J1 = Piezo Speaker
  M3 = DC Motor
  U1 = POT [package=pot_mammoth]
  S1 = H-Bridge with L298N
  Matrix_keypad1 = KEYPAD 4x4
  Part3 = Bluetooth HC-05 Macho
  R1 = Resistor [tolerance=±5% resistance=10k package="0402 [SMD]"]

nets:
  N1: Part1.A4/SDA, Part2.A4/SDA
  N2: Part1.A5/SCL, Part2.A5/SCL
  N3: Part1.ICSP_MISO, Part1.D12/MISO, Matrix_keypad1.col2
  N4: Part1.ICSP_MOSI, Part1.D11_PWM/MOSI, Matrix_keypad1.col3
  N5: Part1.D8, Matrix_keypad1.row2
  N6: Part1.D9_PWM, Matrix_keypad1.row1
  N7: Part1.D10_PWM/SS, Matrix_keypad1.col4
  N8: Part1.D13/SCK, Matrix_keypad1.col1
  N9: Part1.D0/RX, LCD1.DB7
  N10: Part1.D1/TX, LCD1.DB6
  N11: Part1.D2, LCD1.DB5
  N12: Part1.D3_PWM, LCD1.DB4
  N13: Part1.D4, LCD1.E
  N14: Part1.D5_PWM, LCD1.RS
  N15: Part1.D6_PWM, Matrix_keypad1.row4
  N16: Part1.D7, Matrix_keypad1.row3
  5V: Part1.5V, LCD1.VDD
  GND: Part1.GND, Part2.GND, LCD1.VSS, LCD1.LED-, J1.pin1, S1.GND, Part3.GND
  N17: Part2.D9_PWM, J1.pin2
  N18: Part2.D0/RX, Part3.TXD
  N19: Part2.D1/TX, Part3.RXD
  N20: Part2.D2, M3.pin_2
  N21: Part2.D3_PWM, M3.pin_1
  N22: Part2.D4, S1.IN4
  N23: Part2.D5_PWM, S1.IN3
  N24: Part2.D6_PWM, S1.IN2
  N25: Part2.D7, S1.IN1
  5V_2: Part2.5V, S1.5V, Part3.VCC
  N26: M1.pin_2, S1.M1-01
  N27: M2.pin_1, S1.M1-02, S1.M2-02, S1.ENB-5V
  N28: M2.pin_2, S1.M2-01
  N29: LCD1.V0, U1.A
  N30: LCD1.LED+, R1.Pin_1
  N31: U1.E, R1.Pin_0

custom parts:
  H-Bridge with L298N: h-bridge
  KEYPAD 4x4: Matrix keypad 16 buttons, 4 rows x 4 columns
